// Logisim project DSFProjectSimulation.circ as structural Verilog: 1 circuit, main circuit main
module main (
);

  Button B00 ();  // open: out
  Button B01 ();  // open: out
  Button B02 ();  // open: out
  Button B03 ();  // open: out
  Button B04 ();  // open: out
  Button B05 ();  // open: out
  Button B06 ();  // open: out
  Button B07 ();  // open: out
  Button B08 ();  // open: out
  Button B09 ();  // open: out
  // NOT_Gate not_1 is placed but not wired
  D_Flip_Flop d_ff_1 ();  // open: D, clk, Q, Qn, preset, reset
  D_Flip_Flop d_ff_2 ();  // open: D, clk, Q, Qn, preset, reset
  D_Flip_Flop d_ff_3 ();  // open: D, clk, Q, Qn, preset, reset
  D_Flip_Flop d_ff_4 ();  // open: D, clk, Q, Qn, preset, reset
  D_Flip_Flop d_ff_5 ();  // open: D, clk, Q, Qn, preset, reset
  D_Flip_Flop d_ff_6 ();  // open: D, clk, Q, Qn, preset, reset
  D_Flip_Flop d_ff_7 ();  // open: D, clk, Q, Qn, preset, reset
  D_Flip_Flop d_ff_8 ();  // open: D, clk, Q, Qn, preset, reset
  D_Flip_Flop d_ff_9 ();  // open: D, clk, Q, Qn, preset, reset
endmodule
